// Logisim project lab1.circ as structural Verilog: 1 circuit, main circuit main
module main (
  input  x,
  input  s,
  input  y,
  input  a,
  input  b,
  input  c,
  output f1,
  output f2,
  output f22
);

  wire and_1_out, and_2_out, and_3_out, not_1_out, not_2_out, not_3_out, not_4_out, not_5_out, or_1_out,
       or_2_out;

  not not_1 (not_1_out, a);
  not not_2 (not_2_out, s);
  or or_1 (or_1_out, a, b);
  not not_3 (not_3_out, b);
  not not_4 (not_4_out, b);
  or or_2 (or_2_out, not_1_out, c);
  and and_1 (and_1_out, x, not_2_out);
  and and_2 (and_2_out, s, y);
  not not_5 (not_5_out, or_1_out);
  and and_3 (and_3_out, not_3_out, c);
  and and_4 (f22, not_4_out, or_2_out);
  or or_3 (f1, and_1_out, and_2_out);
  or or_4 (f2, not_5_out, and_3_out);

  // Notes on the sheet:
  //   Part 1: f = xs' + ys
  //   Part2: f =(a+b)' + cb'
  //   Cheaper: f = a'b' + cb' = b'(a' + c)
endmodule
