// Logisim project mux.circ as structural Verilog: 10 circuits, main circuit mux2to1
module main (
  input  SW_0,
  input  SW_1,
  input  SW_2,
  input  SW_3,
  input  SW_9,
  input  SW_8,
  output LEDR_9,
  output LEDR_0
);

  wire hex_0_1_hex0, hex_1_1_hex1, hex_2_1_hex2, hex_3_1_hex3, hex_4_1_hex4, hex_5_1_hex5, hex_6_1_hex6;

  mux2to1 u (.x(SW_0), .y(SW_1), .s(SW_9), .m(LEDR_9));
  mux4to1 mux4to1_1 (.u(SW_0), .v(SW_1), .w(SW_2), .x(SW_3), .s0(SW_9), .s1(SW_8), .m(LEDR_0));
  HEX_0 hex_0_1 (.c_3(SW_0), .c_2(SW_1), .c_1(SW_2), .c_0(SW_3), .hex0(hex_0_1_hex0));
  HEX_1 hex_1_1 (.c_3(SW_0), .c_2(SW_1), .c_1(SW_2), .c_0(SW_3), .hex1(hex_1_1_hex1));
  HEX_2 hex_2_1 (.c_3(SW_0), .c_2(SW_1), .c_1(SW_2), .c_0(SW_3), .hex2(hex_2_1_hex2));
  HEX_3 hex_3_1 (.c_3(SW_0), .c_2(SW_1), .c_1(SW_2), .c_0(SW_3), .hex3(hex_3_1_hex3));
  HEX_4 hex_4_1 (.c_3(SW_0), .c_2(SW_1), .c_1(SW_2), .c_0(SW_3), .hex4(hex_4_1_hex4));
  HEX_5 hex_5_1 (.c_3(SW_0), .c_2(SW_1), .c_1(SW_2), .c_0(SW_3), .hex5(hex_5_1_hex5));
  HEX_6 hex_6_1 (.c_3(SW_0), .c_2(SW_1), .c_1(SW_2), .c_0(SW_3), .hex6(hex_6_1_hex6));
  _7_Segment_Display u_7_segment_display_1 (
    .g(hex_6_1_hex6), .f(hex_5_1_hex5), .a(hex_0_1_hex0), .b(hex_1_1_hex1), .e(hex_4_1_hex4),
    .d(hex_3_1_hex3), .c(hex_2_1_hex2));  // open: dp
endmodule

module mux2to1 (
  input  x,
  input  y,
  input  s,
  output m
);

  Multiplexer #(.enable("false")) multiplexer_1 (.in0(x), .in1(y), .out(m), .sel(s));
endmodule

module mux4to1 (
  input  u,
  input  v,
  input  w,
  input  x,
  input  s0,
  input  s1,
  output m
);

  wire mux2to1_1_m, mux2to1_2_m;

  mux2to1 mux2to1_1 (.x(u), .y(v), .s(s0), .m(mux2to1_1_m));
  mux2to1 mux2to1_2 (.x(w), .y(x), .s(s0), .m(mux2to1_2_m));
  mux2to1 mux2to1_3 (.x(mux2to1_1_m), .y(mux2to1_2_m), .s(s1), .m(m));
endmodule

module HEX_0 (
  input  c_3,
  input  c_2,
  input  c_1,
  input  c_0,
  output hex0
);

  wire and_1_out, and_2_out, and_3_out, and_4_out, not_1_out, not_2_out, not_3_out, not_4_out, or_1_out,
       or_2_out;

  not not_1 (not_1_out, c_0);
  not not_2 (not_2_out, c_2);
  not not_3 (not_3_out, c_3);
  or or_1 (or_1_out, c_3, not_2_out);
  or or_2 (or_2_out, not_3_out, c_2);
  not not_4 (not_4_out, c_1);
  and and_1 (and_1_out, not_1_out, or_1_out);
  and and_2 (and_2_out, or_2_out, c_1);
  and and_3 (and_3_out, c_3, not_2_out, not_4_out);
  and and_4 (and_4_out, not_3_out, c_2, c_0);
  or or_3 (hex0, and_1_out, and_2_out, and_3_out, and_4_out);
endmodule

module HEX_1 (
  input  c_3,
  input  c_2,
  input  c_1,
  input  c_0,
  output hex1
);

  wire and_1_out, and_2_out, and_3_out, not_1_out, not_2_out, not_3_out, not_4_out, not_5_out, not_6_out,
       or_1_out, xor_1_out;

  not not_1 (not_1_out, c_2);
  xor xor_1 (xor_1_out, c_1, c_0);
  not not_2 (not_2_out, c_0);
  not not_3 (not_3_out, c_3);
  not not_4 (not_4_out, c_1);
  not not_5 (not_5_out, c_3);
  not not_6 (not_6_out, xor_1_out);
  or or_1 (or_1_out, not_3_out, not_2_out);
  and and_1 (and_1_out, or_1_out, not_1_out);
  and and_2 (and_2_out, c_3, c_0, not_4_out);
  and and_3 (and_3_out, not_5_out, not_6_out);
  or or_2 (hex1, and_1_out, and_2_out, and_3_out);
endmodule

module HEX_2 (
  input  c_3,
  input  c_2,
  input  c_1,
  input  c_0,
  output hex2
);

  wire and_1_out, and_2_out, and_3_out, not_1_out, not_2_out, not_3_out, or_1_out, xor_1_out;

  not not_1 (not_1_out, c_3);
  not not_2 (not_2_out, c_2);
  not not_3 (not_3_out, c_1);
  and and_1 (and_1_out, not_1_out, not_2_out);
  or or_1 (or_1_out, not_3_out, c_0);
  xor xor_1 (xor_1_out, c_3, c_2);
  and and_2 (and_2_out, and_1_out, or_1_out);
  and and_3 (and_3_out, not_3_out, c_0);
  or or_2 (hex2, xor_1_out, and_2_out, and_3_out);
endmodule

module HEX_3 (
  input  c_3,
  input  c_2,
  input  c_1,
  input  c_0,
  output hex3
);

  wire and_1_out, and_2_out, and_3_out, and_4_out, and_5_out, not_1_out, not_2_out, not_3_out, not_4_out,
       or_1_out, xor_1_out;

  not not_1 (not_1_out, c_3);
  not not_2 (not_2_out, c_2);
  not not_3 (not_3_out, c_0);
  not not_4 (not_4_out, c_1);
  and and_1 (and_1_out, not_1_out, not_2_out);
  or or_1 (or_1_out, c_1, not_3_out);
  xor xor_1 (xor_1_out, c_1, c_0);
  and and_2 (and_2_out, not_4_out, c_3);
  and and_3 (and_3_out, and_1_out, or_1_out);
  and and_4 (and_4_out, c_2, xor_1_out);
  and and_5 (and_5_out, c_0, c_3, not_2_out);
  or or_2 (hex3, and_2_out, and_3_out, and_4_out, and_5_out);
endmodule

module HEX_4 (
  input  c_3,
  input  c_2,
  input  c_1,
  input  c_0,
  output hex4
);

  wire and_1_out, and_2_out, not_1_out, not_2_out, or_1_out, or_2_out;

  not not_1 (not_1_out, c_2);
  not not_2 (not_2_out, c_0);
  or or_1 (or_1_out, c_2, c_1);
  or or_2 (or_2_out, not_1_out, c_1);
  and and_1 (and_1_out, c_3, or_1_out);
  and and_2 (and_2_out, or_2_out, not_2_out);
  or or_3 (hex4, and_1_out, and_2_out);
endmodule

module HEX_5 (
  input  c_3,
  input  c_2,
  input  c_1,
  input  c_0,
  output hex5
);

  wire and_1_out, and_2_out, and_3_out, not_1_out, not_2_out, not_3_out, not_4_out, or_1_out, or_2_out;

  not not_1 (not_1_out, c_2);
  not not_2 (not_2_out, c_3);
  not not_3 (not_3_out, c_1);
  not not_4 (not_4_out, c_0);
  or or_1 (or_1_out, not_1_out, c_1);
  or or_2 (or_2_out, c_2, not_3_out);
  and and_1 (and_1_out, c_3, or_1_out);
  and and_2 (and_2_out, not_2_out, c_2, not_3_out);
  and and_3 (and_3_out, or_2_out, not_4_out);
  or or_3 (hex5, and_1_out, and_2_out, and_3_out);
endmodule

module HEX_6 (
  input  c_3,
  input  c_2,
  input  c_1,
  input  c_0,
  output hex6
);

  wire and_1_out, and_2_out, and_3_out, not_1_out, not_2_out, not_3_out, not_4_out, or_1_out, or_2_out;

  not not_1 (not_1_out, c_2);
  not not_2 (not_2_out, c_0);
  or or_1 (or_1_out, not_1_out, c_0);
  or or_2 (or_2_out, not_1_out, not_2_out);
  not not_3 (not_3_out, c_3);
  not not_4 (not_4_out, c_1);
  and and_1 (and_1_out, c_3, or_1_out);
  and and_2 (and_2_out, not_3_out, c_2, not_4_out);
  and and_3 (and_3_out, c_1, or_2_out);
  or or_3 (hex6, and_1_out, and_2_out, and_3_out);
endmodule
