// Logisim project Lab7.circ as structural Verilog
module RAM32 (
  input  [4:0] Address,
  input  write_en,
  input  [3:0] data_in,
  input  Reset
);

  wire clock_1_out, register_2_q, undriven;
  wire [3:0] ram_1_dout, register_3_q;
  wire [4:0] register_1_q;

  Clock clock_1 (.out(clock_1_out));
  Register #(.width(5)) register_1 (.D(Address), .en(undriven), .clk(clock_1_out), .Q(register_1_q), .clr(Reset));
  Register #(.width(1)) register_2 (.D(write_en), .clk(clock_1_out), .Q(register_2_q), .clr(Reset));  // open: en
  Register #(.width(4)) register_3 (.D(data_in), .clk(clock_1_out), .Q(register_3_q), .clr(Reset));  // open: en
  RAM #(.addrWidth(5), .dataWidth(4)) ram_1 (
    .addr(register_1_q), .we(register_2_q), .oe(1'b1), .clk(clock_1_out), .din(register_3_q),
    .dout(ram_1_dout));
  Hex_Digit_Display hex_digit_display_1 (.value(ram_1_dout));  // open: dp
endmodule

module P1q3 (
  input  write_en,
  input  Reset
);

  wire clock_1_out, register_2_q, undriven;
  wire [3:0] counter_2_q, ram_1_dout, register_3_q;
  wire [4:0] counter_1_q, register_1_q;

  Clock clock_1 (.out(clock_1_out));
  Counter #(.max('h1f), .width(5)) counter_1 (
    .clr(Reset), .clk(clock_1_out), .Q(counter_1_q));  // open: load, up, count, D, carry
  Counter #(.max('hf), .width(4)) counter_2 (
    .clr(Reset), .clk(clock_1_out), .Q(counter_2_q));  // open: load, up, count, D, carry
  Register #(.width(5)) register_1 (.D(counter_1_q), .en(undriven), .clk(clock_1_out), .Q(register_1_q), .clr(Reset));
  Register #(.width(1)) register_2 (.D(write_en), .clk(clock_1_out), .Q(register_2_q), .clr(Reset));  // open: en
  Register #(.width(4)) register_3 (.D(counter_2_q), .clk(clock_1_out), .Q(register_3_q), .clr(Reset));  // open: en
  RAM #(.addrWidth(5), .dataWidth(4)) ram_1 (
    .addr(register_1_q), .we(register_2_q), .oe(1'b1), .clk(clock_1_out), .din(register_3_q),
    .dout(ram_1_dout));
  Hex_Digit_Display hex_digit_display_1 (.value(ram_1_dout));  // open: dp
endmodule

module DATAPATH (
  input  [6:0] Y_cordiante,
  input  enable,
  input  [6:0] X_cordinate,
  input  Clock,
  input  Reset,
  output [6:0] y_cordinate_out,
  output [6:0] x_cordinate_out,
  output [23:0] RGB
);

  wire counter_1_carry, not_1_out, register_1_q;
  wire [3:0] counter_1_q, counter_3_q;
  wire [6:0] bit_extender_1_out, bit_extender_2_out;

  not not_1 (not_1_out, enable);
  Counter #(.max('hf), .width(4)) counter_1 (
    .clr(Reset), .load(not_1_out), .clk(Clock), .D(4'b0000), .carry(counter_1_carry), .Q(counter_1_q));  // open: up, count
  Counter #(.max('hffff), .ongoal("load"), .width(24)) counter_2 (
    .clr(Reset), .up(1'b0), .clk(Clock), .D(24'hffff), .Q(RGB));  // open: load, count, carry
  Register #(.width(1)) register_1 (.D(counter_1_carry), .clk(Clock), .Q(register_1_q), .clr(Reset));  // open: en
  Counter #(.max('hf), .width(4)) counter_3 (
    .clr(Reset), .load(not_1_out), .clk(register_1_q), .D(4'b0000), .Q(counter_3_q));  // open: up, count, carry
  assign bit_extender_1_out = {{3{1'b0}}, counter_1_q};  // Bit_Extender bit_extender_1
  Adder #(.width(7)) adder_1 (.a(bit_extender_1_out), .b(X_cordinate), .out(x_cordinate_out));  // open: cin, cout
  assign bit_extender_2_out = {{3{1'b0}}, counter_3_q};  // Bit_Extender bit_extender_2
  Adder #(.width(7)) adder_2 (.a(Y_cordiante), .b(bit_extender_2_out), .out(y_cordinate_out));  // open: cin, cout
endmodule

module PART2 (
  input  write_en,
  input  Reset,
  input  [6:0] x,
  input  [6:0] y
);

  wire clock_1_out;
  wire [6:0] datapath_1_x_cordinate_out, datapath_1_y_cordinate_out;
  wire [23:0] datapath_1_rgb;

  Clock clock_1 (.out(clock_1_out));
  DATAPATH datapath_1 (
    .Y_cordiante(y), .enable(write_en), .X_cordinate(x), .Clock(clock_1_out), .Reset(Reset),
    .y_cordinate_out(datapath_1_y_cordinate_out), .x_cordinate_out(datapath_1_x_cordinate_out),
    .RGB(datapath_1_rgb));
  // RGB_Video rgb_video_1: pin names not known; wires that end beside it: Reset, clock_1_out, write_en, datapath_1_x_cordinate_out, datapath_1_y_cordinate_out, datapath_1_rgb
endmodule
