// Logisim project LAB3.circ as structural Verilog: 20 circuits, main circuit mux2to1
module main (
  input  [3:0] A,
  input  [2:0] C,
  input  [3:0] B,
  output [7:0] out_4
);

  wire [6:0] hex_display_1_out_2, hex_display_2_out_2, High4_out_2, Low4_out_2;
  wire [7:0] operation0_1_aluout, operation1_1_aluout, operation2_1_aluout, operation3_1_aluout,
       operation4_1_aluout, operation5_1_aluout;

  _7_Segment_Display u_7_segment_display_1 (
    .g(hex_display_2_out_2[6]), .f(hex_display_2_out_2[5]), .a(hex_display_2_out_2[0]),
    .b(hex_display_2_out_2[1]), .e(hex_display_2_out_2[4]), .d(hex_display_2_out_2[3]),
    .c(hex_display_2_out_2[2]));  // open: dp
  _7_Segment_Display u_7_segment_display_2 (
    .g(hex_display_1_out_2[6]), .f(hex_display_1_out_2[5]), .a(hex_display_1_out_2[0]),
    .b(hex_display_1_out_2[1]), .e(hex_display_1_out_2[4]), .d(hex_display_1_out_2[3]),
    .c(hex_display_1_out_2[2]));  // open: dp
  HEX_Display hex_display_1 (.A(A), .out_2(hex_display_1_out_2));
  HEX_Display hex_display_2 (.A(B), .out_2(hex_display_2_out_2));
  operation0 operation0_1 (.A(A), .ALUout(operation0_1_aluout));
  operation1 operation1_1 (.A(A), .B(B), .ALUout(operation1_1_aluout));
  operation2 operation2_1 (.A(A), .B(B), .ALUout(operation2_1_aluout));
  operation3 operation3_1 (.A(A), .B(B), .ALUout(operation3_1_aluout));
  operation4 operation4_1 (.A(A), .B(B), .ALUout(operation4_1_aluout));
  operation5 operation5_1 (.B(B), .A(A), .ALUout(operation5_1_aluout));
  Multiplexer #(.enable("false"), .select(3), .width(8)) multiplexer_1 (
    .in0(operation0_1_aluout), .in1(operation1_1_aluout), .in2(operation2_1_aluout),
    .in3(operation3_1_aluout), .in4(operation4_1_aluout), .in5(operation5_1_aluout), .out(out_4), .sel(C));  // open: in6, in7
  LED led_1 (.in(out_4[0]));
  LED led_2 (.in(out_4[1]));
  LED led_3 (.in(out_4[2]));
  LED led_4 (.in(out_4[3]));
  LED led_5 (.in(out_4[4]));
  LED led_6 (.in(out_4[5]));
  LED led_7 (.in(out_4[6]));
  LED led_8 (.in(out_4[7]));
  HEX_Display Low4 (.A(out_4[3:0]), .out_2(Low4_out_2));
  HEX_Display High4 (.A(out_4[7:4]), .out_2(High4_out_2));
  _7_Segment_Display u_7_segment_display_3 (
    .g(Low4_out_2[6]), .f(Low4_out_2[5]), .a(Low4_out_2[0]), .b(Low4_out_2[1]), .e(Low4_out_2[4]),
    .d(Low4_out_2[3]), .c(Low4_out_2[2]));  // open: dp
  _7_Segment_Display u_7_segment_display_4 (
    .g(High4_out_2[6]), .f(High4_out_2[5]), .a(High4_out_2[0]), .b(High4_out_2[1]), .e(High4_out_2[4]),
    .d(High4_out_2[3]), .c(High4_out_2[2]));  // open: dp
endmodule

module mux2to1 (
  input  x,
  input  y,
  input  s,
  output m
);

  Multiplexer #(.enable("false")) multiplexer_1 (.in0(x), .in1(y), .out(m), .sel(s));
endmodule

module mux4to1 (
  input  u,
  input  v,
  input  w,
  input  x,
  input  s0,
  input  s1,
  output m
);

  wire mux2to1_1_m, mux2to1_2_m;

  mux2to1 mux2to1_1 (.x(u), .y(v), .s(s0), .m(mux2to1_1_m));
  mux2to1 mux2to1_2 (.x(w), .y(x), .s(s0), .m(mux2to1_2_m));
  mux2to1 mux2to1_3 (.x(mux2to1_1_m), .y(mux2to1_2_m), .s(s1), .m(m));
endmodule

module HEX_0 (
  input  c_3,
  input  c_2,
  input  c_1,
  input  c_0,
  output hex0
);

  wire and_1_out, and_2_out, and_3_out, and_4_out, not_1_out, not_2_out, not_3_out, not_4_out, or_1_out,
       or_2_out;

  not not_1 (not_1_out, c_0);
  not not_2 (not_2_out, c_2);
  not not_3 (not_3_out, c_3);
  or or_1 (or_1_out, c_3, not_2_out);
  or or_2 (or_2_out, not_3_out, c_2);
  not not_4 (not_4_out, c_1);
  and and_1 (and_1_out, not_1_out, or_1_out);
  and and_2 (and_2_out, or_2_out, c_1);
  and and_3 (and_3_out, c_3, not_2_out, not_4_out);
  and and_4 (and_4_out, not_3_out, c_2, c_0);
  or or_3 (hex0, and_1_out, and_2_out, and_3_out, and_4_out);
endmodule

module HEX_1 (
  input  c_3,
  input  c_2,
  input  c_1,
  input  c_0,
  output hex1
);

  wire and_1_out, and_2_out, and_3_out, not_1_out, not_2_out, not_3_out, not_4_out, not_5_out, not_6_out,
       or_1_out, xor_1_out;

  not not_1 (not_1_out, c_2);
  xor xor_1 (xor_1_out, c_1, c_0);
  not not_2 (not_2_out, c_0);
  not not_3 (not_3_out, c_3);
  not not_4 (not_4_out, c_1);
  not not_5 (not_5_out, c_3);
  not not_6 (not_6_out, xor_1_out);
  or or_1 (or_1_out, not_3_out, not_2_out);
  and and_1 (and_1_out, or_1_out, not_1_out);
  and and_2 (and_2_out, c_3, c_0, not_4_out);
  and and_3 (and_3_out, not_5_out, not_6_out);
  or or_2 (hex1, and_1_out, and_2_out, and_3_out);
endmodule

module HEX_2 (
  input  c_3,
  input  c_2,
  input  c_1,
  input  c_0,
  output hex2
);

  wire and_1_out, and_2_out, and_3_out, not_1_out, not_2_out, not_3_out, or_1_out, xor_1_out;

  not not_1 (not_1_out, c_3);
  not not_2 (not_2_out, c_2);
  not not_3 (not_3_out, c_1);
  and and_1 (and_1_out, not_1_out, not_2_out);
  or or_1 (or_1_out, not_3_out, c_0);
  xor xor_1 (xor_1_out, c_3, c_2);
  and and_2 (and_2_out, and_1_out, or_1_out);
  and and_3 (and_3_out, not_3_out, c_0);
  or or_2 (hex2, xor_1_out, and_2_out, and_3_out);
endmodule

module HEX_3 (
  input  c_3,
  input  c_2,
  input  c_1,
  input  c_0,
  output hex3
);

  wire and_1_out, and_2_out, and_3_out, and_4_out, and_5_out, not_1_out, not_2_out, not_3_out, not_4_out,
       or_1_out, xor_1_out;

  not not_1 (not_1_out, c_3);
  not not_2 (not_2_out, c_2);
  not not_3 (not_3_out, c_0);
  not not_4 (not_4_out, c_1);
  and and_1 (and_1_out, not_1_out, not_2_out);
  or or_1 (or_1_out, c_1, not_3_out);
  xor xor_1 (xor_1_out, c_1, c_0);
  and and_2 (and_2_out, not_4_out, c_3);
  and and_3 (and_3_out, and_1_out, or_1_out);
  and and_4 (and_4_out, c_2, xor_1_out);
  and and_5 (and_5_out, c_0, c_3, not_2_out);
  or or_2 (hex3, and_2_out, and_3_out, and_4_out, and_5_out);
endmodule

module HEX_4 (
  input  c_3,
  input  c_2,
  input  c_1,
  input  c_0,
  output hex4
);

  wire and_1_out, and_2_out, not_1_out, not_2_out, or_1_out, or_2_out;

  not not_1 (not_1_out, c_2);
  not not_2 (not_2_out, c_0);
  or or_1 (or_1_out, c_2, c_1);
  or or_2 (or_2_out, not_1_out, c_1);
  and and_1 (and_1_out, c_3, or_1_out);
  and and_2 (and_2_out, or_2_out, not_2_out);
  or or_3 (hex4, and_1_out, and_2_out);
endmodule

module HEX_5 (
  input  c_3,
  input  c_2,
  input  c_1,
  input  c_0,
  output hex5
);

  wire and_1_out, and_2_out, and_3_out, not_1_out, not_2_out, not_3_out, not_4_out, or_1_out, or_2_out;

  not not_1 (not_1_out, c_2);
  not not_2 (not_2_out, c_3);
  not not_3 (not_3_out, c_1);
  not not_4 (not_4_out, c_0);
  or or_1 (or_1_out, not_1_out, c_1);
  or or_2 (or_2_out, c_2, not_3_out);
  and and_1 (and_1_out, c_3, or_1_out);
  and and_2 (and_2_out, not_2_out, c_2, not_3_out);
  and and_3 (and_3_out, or_2_out, not_4_out);
  or or_3 (hex5, and_1_out, and_2_out, and_3_out);
endmodule

module HEX_6 (
  input  c_3,
  input  c_2,
  input  c_1,
  input  c_0,
  output hex6
);

  wire and_1_out, and_2_out, and_3_out, not_1_out, not_2_out, not_3_out, not_4_out, or_1_out, or_2_out;

  not not_1 (not_1_out, c_2);
  not not_2 (not_2_out, c_0);
  or or_1 (or_1_out, not_1_out, c_0);
  or or_2 (or_2_out, not_1_out, not_2_out);
  not not_3 (not_3_out, c_3);
  not not_4 (not_4_out, c_1);
  and and_1 (and_1_out, c_3, or_1_out);
  and and_2 (and_2_out, not_3_out, c_2, not_4_out);
  and and_3 (and_3_out, c_1, or_2_out);
  or or_3 (hex6, and_1_out, and_2_out, and_3_out);
endmodule

module mux7 (
  input  [9:0] SW9_0,
  output LEDR0
);

  Multiplexer #(.enable("false"), .select(3)) multiplexer_1 (
    .in0(SW9_0[0]), .in1(SW9_0[1]), .in2(SW9_0[2]), .in3(SW9_0[3]), .in4(SW9_0[4]), .in5(SW9_0[5]),
    .in6(SW9_0[6]), .out(LEDR0), .sel(SW9_0[9:7]));  // open: in7
endmodule

module FA (
  input  c_in,
  input  a,
  input  b,
  output s,
  output c_out
);

  wire xor_1_out;

  xor xor_1 (xor_1_out, a, b);
  Multiplexer #(.enable("false")) multiplexer_1 (.in0(b), .in1(c_in), .out(c_out), .sel(xor_1_out));
  xor xor_2 (s, c_in, xor_1_out);
endmodule

module p2 (
  input  [8:0] SW8_0,
  output LEDR0,
  output LEDR1,
  output LEDR2,
  output LEDR3,
  output LEDR4
);

  wire fa_1_c_out, fa_2_c_out, fa_3_c_out;

  FA fa_1 (.c_in(SW8_0[8]), .a(SW8_0[0]), .b(SW8_0[4]), .s(LEDR0), .c_out(fa_1_c_out));
  FA fa_2 (.c_in(fa_1_c_out), .a(SW8_0[1]), .b(SW8_0[5]), .s(LEDR1), .c_out(fa_2_c_out));
  FA fa_3 (.c_in(fa_2_c_out), .a(SW8_0[2]), .b(SW8_0[6]), .s(LEDR2), .c_out(fa_3_c_out));
  FA fa_4 (.c_in(fa_3_c_out), .a(SW8_0[3]), .b(SW8_0[7]), .s(LEDR3), .c_out(LEDR4));
endmodule

module operation0 (
  input  [3:0] A,
  output [7:0] ALUout
);

  wire [4:0] p2_1_ledr0;

  p2 p2_1 (
    .SW8_0({5'b10000, A}), .LEDR0(p2_1_ledr0[0]), .LEDR1(p2_1_ledr0[1]), .LEDR2(p2_1_ledr0[2]),
    .LEDR3(p2_1_ledr0[3]), .LEDR4(p2_1_ledr0[4]));
  assign ALUout = {{3{1'b0}}, p2_1_ledr0};  // Bit_Extender bit_extender_1
endmodule

module operation1 (
  input  [3:0] A,
  input  [3:0] B,
  output [7:0] ALUout
);

  wire [4:0] p2_1_ledr0;

  p2 p2_1 (
    .SW8_0({1'b0, B, A}), .LEDR0(p2_1_ledr0[0]), .LEDR1(p2_1_ledr0[1]), .LEDR2(p2_1_ledr0[2]),
    .LEDR3(p2_1_ledr0[3]), .LEDR4(p2_1_ledr0[4]));
  assign ALUout = {{3{1'b0}}, p2_1_ledr0};  // Bit_Extender bit_extender_1
endmodule

module operation2 (
  input  [3:0] A,
  input  [3:0] B,
  output [7:0] ALUout
);

  wire adder_1_cout, adder_2_cout, adder_3_cout;
  wire [4:0] adder_1_out;

  Adder #(.width(1)) adder_1 (.a(A[0]), .b(B[0]), .out(adder_1_out[0]), .cin(1'b0), .cout(adder_1_cout));
  Adder #(.width(1)) adder_2 (.a(A[1]), .b(B[1]), .out(adder_1_out[1]), .cin(adder_1_cout), .cout(adder_2_cout));
  Adder #(.width(1)) adder_3 (.a(A[2]), .b(B[2]), .out(adder_1_out[2]), .cin(adder_2_cout), .cout(adder_3_cout));
  Adder #(.width(1)) adder_4 (.a(A[3]), .b(B[3]), .out(adder_1_out[3]), .cin(adder_3_cout), .cout(adder_1_out[4]));
  assign ALUout = {{3{1'b0}}, adder_1_out};  // Bit_Extender bit_extender_1
endmodule

module operation3 (
  input  [3:0] A,
  input  [3:0] B,
  output [7:0] ALUout
);

  xor xor_1 (ALUout[0], A[0], B[0]);
  xor xor_2 (ALUout[1], A[1], B[1]);
  xor xor_3 (ALUout[2], A[2], B[2]);
  xor xor_4 (ALUout[3], A[3], B[3]);
  or or_1 (ALUout[4], A[0], B[0]);
  or or_2 (ALUout[5], A[1], B[1]);
  or or_3 (ALUout[6], A[2], B[2]);
  or or_4 (ALUout[7], A[3], B[3]);
endmodule

module operation4 (
  input  [3:0] A,
  input  [3:0] B,
  output [7:0] ALUout
);

  wire or_1_out;

  or or_1 (or_1_out, A[0], A[1], A[2], A[3], B[0], B[1], B[2], B[3]);
  assign ALUout = {{7{1'b0}}, or_1_out};  // Bit_Extender bit_extender_1
endmodule

module operation5 (
  input  [3:0] B,
  input  [3:0] A,
  output [7:0] ALUout
);


  assign ALUout = {A, B};
endmodule

module HEX_Display (
  input  [3:0] A,
  output [6:0] out_2
);

  HEX_0 hex_0_1 (.c_3(A[3]), .c_2(A[2]), .c_1(A[1]), .c_0(A[0]), .hex0(out_2[0]));
  HEX_1 hex_1_1 (.c_3(A[3]), .c_2(A[2]), .c_1(A[1]), .c_0(A[0]), .hex1(out_2[1]));
  HEX_2 hex_2_1 (.c_3(A[3]), .c_2(A[2]), .c_1(A[1]), .c_0(A[0]), .hex2(out_2[2]));
  HEX_3 hex_3_1 (.c_3(A[3]), .c_2(A[2]), .c_1(A[1]), .c_0(A[0]), .hex3(out_2[3]));
  HEX_4 hex_4_1 (.c_3(A[3]), .c_2(A[2]), .c_1(A[1]), .c_0(A[0]), .hex4(out_2[4]));
  HEX_5 hex_5_1 (.c_3(A[3]), .c_2(A[2]), .c_1(A[1]), .c_0(A[0]), .hex5(out_2[5]));
  HEX_6 hex_6_1 (.c_3(A[3]), .c_2(A[2]), .c_1(A[1]), .c_0(A[0]), .hex6(out_2[6]));
endmodule
