// Logisim project LAB4.circ as structural Verilog: 24 circuits, main circuit HEX_0
module HEX_0 (
  input  c_3,
  input  c_2,
  input  c_1,
  input  c_0,
  output hex0
);

  wire and_1_out, and_2_out, and_3_out, and_4_out, not_1_out, not_2_out, not_3_out, not_4_out, or_1_out,
       or_2_out;

  not not_1 (not_1_out, c_0);
  not not_2 (not_2_out, c_2);
  not not_3 (not_3_out, c_3);
  or or_1 (or_1_out, c_3, not_2_out);
  or or_2 (or_2_out, not_3_out, c_2);
  not not_4 (not_4_out, c_1);
  and and_1 (and_1_out, not_1_out, or_1_out);
  and and_2 (and_2_out, or_2_out, c_1);
  and and_3 (and_3_out, c_3, not_2_out, not_4_out);
  and and_4 (and_4_out, not_3_out, c_2, c_0);
  or or_3 (hex0, and_1_out, and_2_out, and_3_out, and_4_out);
endmodule

module HEX_1 (
  input  c_3,
  input  c_2,
  input  c_1,
  input  c_0,
  output hex1
);

  wire and_1_out, and_2_out, and_3_out, not_1_out, not_2_out, not_3_out, not_4_out, not_5_out, not_6_out,
       or_1_out, xor_1_out;

  not not_1 (not_1_out, c_2);
  xor xor_1 (xor_1_out, c_1, c_0);
  not not_2 (not_2_out, c_0);
  not not_3 (not_3_out, c_3);
  not not_4 (not_4_out, c_1);
  not not_5 (not_5_out, c_3);
  not not_6 (not_6_out, xor_1_out);
  or or_1 (or_1_out, not_3_out, not_2_out);
  and and_1 (and_1_out, or_1_out, not_1_out);
  and and_2 (and_2_out, c_3, c_0, not_4_out);
  and and_3 (and_3_out, not_5_out, not_6_out);
  or or_2 (hex1, and_1_out, and_2_out, and_3_out);
endmodule

module HEX_2 (
  input  c_3,
  input  c_2,
  input  c_1,
  input  c_0,
  output hex2
);

  wire and_1_out, and_2_out, and_3_out, not_1_out, not_2_out, not_3_out, or_1_out, xor_1_out;

  not not_1 (not_1_out, c_3);
  not not_2 (not_2_out, c_2);
  not not_3 (not_3_out, c_1);
  and and_1 (and_1_out, not_1_out, not_2_out);
  or or_1 (or_1_out, not_3_out, c_0);
  xor xor_1 (xor_1_out, c_3, c_2);
  and and_2 (and_2_out, and_1_out, or_1_out);
  and and_3 (and_3_out, not_3_out, c_0);
  or or_2 (hex2, xor_1_out, and_2_out, and_3_out);
endmodule

module HEX_3 (
  input  c_3,
  input  c_2,
  input  c_1,
  input  c_0,
  output hex3
);

  wire and_1_out, and_2_out, and_3_out, and_4_out, and_5_out, not_1_out, not_2_out, not_3_out, not_4_out,
       or_1_out, xor_1_out;

  not not_1 (not_1_out, c_3);
  not not_2 (not_2_out, c_2);
  not not_3 (not_3_out, c_0);
  not not_4 (not_4_out, c_1);
  and and_1 (and_1_out, not_1_out, not_2_out);
  or or_1 (or_1_out, c_1, not_3_out);
  xor xor_1 (xor_1_out, c_1, c_0);
  and and_2 (and_2_out, not_4_out, c_3);
  and and_3 (and_3_out, and_1_out, or_1_out);
  and and_4 (and_4_out, c_2, xor_1_out);
  and and_5 (and_5_out, c_0, c_3, not_2_out);
  or or_2 (hex3, and_2_out, and_3_out, and_4_out, and_5_out);
endmodule

module HEX_4 (
  input  c_3,
  input  c_2,
  input  c_1,
  input  c_0,
  output hex4
);

  wire and_1_out, and_2_out, not_1_out, not_2_out, or_1_out, or_2_out;

  not not_1 (not_1_out, c_2);
  not not_2 (not_2_out, c_0);
  or or_1 (or_1_out, c_2, c_1);
  or or_2 (or_2_out, not_1_out, c_1);
  and and_1 (and_1_out, c_3, or_1_out);
  and and_2 (and_2_out, or_2_out, not_2_out);
  or or_3 (hex4, and_1_out, and_2_out);
endmodule

module HEX_5 (
  input  c_3,
  input  c_2,
  input  c_1,
  input  c_0,
  output hex5
);

  wire and_1_out, and_2_out, and_3_out, not_1_out, not_2_out, not_3_out, not_4_out, or_1_out, or_2_out;

  not not_1 (not_1_out, c_2);
  not not_2 (not_2_out, c_3);
  not not_3 (not_3_out, c_1);
  not not_4 (not_4_out, c_0);
  or or_1 (or_1_out, not_1_out, c_1);
  or or_2 (or_2_out, c_2, not_3_out);
  and and_1 (and_1_out, c_3, or_1_out);
  and and_2 (and_2_out, not_2_out, c_2, not_3_out);
  and and_3 (and_3_out, or_2_out, not_4_out);
  or or_3 (hex5, and_1_out, and_2_out, and_3_out);
endmodule

module HEX_6 (
  input  c_3,
  input  c_2,
  input  c_1,
  input  c_0,
  output hex6
);

  wire and_1_out, and_2_out, and_3_out, not_1_out, not_2_out, not_3_out, not_4_out, or_1_out, or_2_out;

  not not_1 (not_1_out, c_2);
  not not_2 (not_2_out, c_0);
  or or_1 (or_1_out, not_1_out, c_0);
  or or_2 (or_2_out, not_1_out, not_2_out);
  not not_3 (not_3_out, c_3);
  not not_4 (not_4_out, c_1);
  and and_1 (and_1_out, c_3, or_1_out);
  and and_2 (and_2_out, not_3_out, c_2, not_4_out);
  and and_3 (and_3_out, c_1, or_2_out);
  or or_3 (hex6, and_1_out, and_2_out, and_3_out);
endmodule

module mux7 (
  input  [9:0] SW9_0,
  output LEDR0
);

  Multiplexer #(.enable("false"), .select(3)) multiplexer_1 (
    .in0(SW9_0[0]), .in1(SW9_0[1]), .in2(SW9_0[2]), .in3(SW9_0[3]), .in4(SW9_0[4]), .in5(SW9_0[5]),
    .in6(SW9_0[6]), .out(LEDR0), .sel(SW9_0[9:7]));  // open: in7
endmodule

module FA (
  input  c_in,
  input  a,
  input  b,
  output s,
  output c_out
);

  wire xor_1_out;

  xor xor_1 (xor_1_out, a, b);
  Multiplexer #(.enable("false")) multiplexer_1 (.in0(b), .in1(c_in), .out(c_out), .sel(xor_1_out));
  xor xor_2 (s, c_in, xor_1_out);
endmodule

module p2 (
  input  [8:0] SW8_0,
  output LEDR0,
  output LEDR1,
  output LEDR2,
  output LEDR3,
  output LEDR4
);

  wire fa_1_c_out, fa_2_c_out, fa_3_c_out;

  FA fa_1 (.c_in(SW8_0[8]), .a(SW8_0[0]), .b(SW8_0[4]), .s(LEDR0), .c_out(fa_1_c_out));
  FA fa_2 (.c_in(fa_1_c_out), .a(SW8_0[1]), .b(SW8_0[5]), .s(LEDR1), .c_out(fa_2_c_out));
  FA fa_3 (.c_in(fa_2_c_out), .a(SW8_0[2]), .b(SW8_0[6]), .s(LEDR2), .c_out(fa_3_c_out));
  FA fa_4 (.c_in(fa_3_c_out), .a(SW8_0[3]), .b(SW8_0[7]), .s(LEDR3), .c_out(LEDR4));
endmodule

module operation0 (
  input  [3:0] A,
  output [7:0] ALUout
);

  wire [4:0] p2_1_ledr0;

  p2 p2_1 (
    .SW8_0({5'b10000, A}), .LEDR0(p2_1_ledr0[0]), .LEDR1(p2_1_ledr0[1]), .LEDR2(p2_1_ledr0[2]),
    .LEDR3(p2_1_ledr0[3]), .LEDR4(p2_1_ledr0[4]));
  assign ALUout = {{3{1'b0}}, p2_1_ledr0};  // Bit_Extender bit_extender_1
endmodule

module operation1 (
  input  [3:0] A,
  input  [3:0] B,
  output [7:0] ALUout
);

  wire [4:0] p2_1_ledr0;

  p2 p2_1 (
    .SW8_0({1'b0, B, A}), .LEDR0(p2_1_ledr0[0]), .LEDR1(p2_1_ledr0[1]), .LEDR2(p2_1_ledr0[2]),
    .LEDR3(p2_1_ledr0[3]), .LEDR4(p2_1_ledr0[4]));
  assign ALUout = {{3{1'b0}}, p2_1_ledr0};  // Bit_Extender bit_extender_1
endmodule

module operation2 (
  input  [3:0] A,
  input  [3:0] B,
  output [7:0] ALUout
);

  wire adder_1_cout, adder_2_cout, adder_3_cout;
  wire [4:0] adder_1_out;

  Adder #(.width(1)) adder_1 (.a(A[0]), .b(B[0]), .out(adder_1_out[0]), .cin(1'b0), .cout(adder_1_cout));
  Adder #(.width(1)) adder_2 (.a(A[1]), .b(B[1]), .out(adder_1_out[1]), .cin(adder_1_cout), .cout(adder_2_cout));
  Adder #(.width(1)) adder_3 (.a(A[2]), .b(B[2]), .out(adder_1_out[2]), .cin(adder_2_cout), .cout(adder_3_cout));
  Adder #(.width(1)) adder_4 (.a(A[3]), .b(B[3]), .out(adder_1_out[3]), .cin(adder_3_cout), .cout(adder_1_out[4]));
  assign ALUout = {{3{1'b0}}, adder_1_out};  // Bit_Extender bit_extender_1
endmodule

module operation3 (
  input  [3:0] A,
  input  [3:0] B,
  output [7:0] ALUout
);

  xor xor_1 (ALUout[0], A[0], B[0]);
  xor xor_2 (ALUout[1], A[1], B[1]);
  xor xor_3 (ALUout[2], A[2], B[2]);
  xor xor_4 (ALUout[3], A[3], B[3]);
  or or_1 (ALUout[4], A[0], B[0]);
  or or_2 (ALUout[5], A[1], B[1]);
  or or_3 (ALUout[6], A[2], B[2]);
  or or_4 (ALUout[7], A[3], B[3]);
endmodule

module operation4 (
  input  [3:0] A,
  input  [3:0] B,
  output [7:0] ALUout
);

  wire or_1_out;

  or or_1 (or_1_out, A[0], A[1], A[2], A[3], B[0], B[1], B[2], B[3]);
  assign ALUout = {{7{1'b0}}, or_1_out};  // Bit_Extender bit_extender_1
endmodule

module HEX_Display (
  input  [3:0] A,
  output [6:0] out_2
);

  HEX_0 hex_0_1 (.c_3(A[3]), .c_2(A[2]), .c_1(A[1]), .c_0(A[0]), .hex0(out_2[0]));
  HEX_1 hex_1_1 (.c_3(A[3]), .c_2(A[2]), .c_1(A[1]), .c_0(A[0]), .hex1(out_2[1]));
  HEX_2 hex_2_1 (.c_3(A[3]), .c_2(A[2]), .c_1(A[1]), .c_0(A[0]), .hex2(out_2[2]));
  HEX_3 hex_3_1 (.c_3(A[3]), .c_2(A[2]), .c_1(A[1]), .c_0(A[0]), .hex3(out_2[3]));
  HEX_4 hex_4_1 (.c_3(A[3]), .c_2(A[2]), .c_1(A[1]), .c_0(A[0]), .hex4(out_2[4]));
  HEX_5 hex_5_1 (.c_3(A[3]), .c_2(A[2]), .c_1(A[1]), .c_0(A[0]), .hex5(out_2[5]));
  HEX_6 hex_6_1 (.c_3(A[3]), .c_2(A[2]), .c_1(A[1]), .c_0(A[0]), .hex6(out_2[6]));
endmodule

module newoperation5 (
  input  [3:0] B,
  input  [3:0] A,
  output [7:0] ALUout
);

  wire [2:0] bit_extender_2_out;
  wire [7:0] bit_extender_1_out;

  assign bit_extender_1_out = {{4{B[3]}}, B};  // Bit_Extender bit_extender_1
  Bit_Extender #(.in_width(4), .out_width(3), .\type ("zero")) bit_extender_2 (.in(A), .out(bit_extender_2_out));
  Shifter shifter_1 (.in(bit_extender_1_out), .\dist (bit_extender_2_out), .out(ALUout));
endmodule

module operation6 (
  input  [3:0] B,
  input  [3:0] A,
  output [7:0] ALUout
);

  wire [2:0] bit_extender_2_out;
  wire [7:0] bit_extender_1_out;

  assign bit_extender_1_out = {{4{B[3]}}, B};  // Bit_Extender bit_extender_1
  Bit_Extender #(.in_width(4), .out_width(3)) bit_extender_2 (.in(A), .out(bit_extender_2_out));
  Shifter #(.shift("lr")) shifter_1 (.in(bit_extender_1_out), .\dist (bit_extender_2_out), .out(ALUout));
endmodule

module operation7 (
  input  [3:0] B,
  input  [3:0] A,
  output [7:0] ALUout
);

  wire [7:0] bit_extender_1_out, bit_extender_2_out;

  assign bit_extender_1_out = {{4{1'b0}}, B};  // Bit_Extender bit_extender_1
  assign bit_extender_2_out = {{4{1'b0}}, A};  // Bit_Extender bit_extender_2
  Multiplier multiplier_1 (.a(bit_extender_1_out), .b(bit_extender_2_out), .out(ALUout));  // open: cin, cout
endmodule

module part2 (
  input  [3:0] A,
  input  ClearSignals,
  input  Clock,
  input  Reset,
  input  [2:0] C,
  output [7:0] ALUout
);

  wire [6:0] hex_display_1_out_2, hex_display_2_out_2, High4_out_2, Low4_out_2;
  wire [7:0] multiplexer_1_out, newoperation5_1_aluout, operation0_1_aluout, operation1_1_aluout,
       operation2_1_aluout, operation3_1_aluout, operation4_1_aluout, operation6_1_aluout,
       operation7_1_aluout;

  _7_Segment_Display u_7_segment_display_1 (
    .g(hex_display_2_out_2[6]), .f(hex_display_2_out_2[5]), .a(hex_display_2_out_2[0]),
    .b(hex_display_2_out_2[1]), .e(hex_display_2_out_2[4]), .d(hex_display_2_out_2[3]),
    .c(hex_display_2_out_2[2]));  // open: dp
  _7_Segment_Display u_7_segment_display_2 (
    .g(hex_display_1_out_2[6]), .f(hex_display_1_out_2[5]), .a(hex_display_1_out_2[0]),
    .b(hex_display_1_out_2[1]), .e(hex_display_1_out_2[4]), .d(hex_display_1_out_2[3]),
    .c(hex_display_1_out_2[2]));  // open: dp
  HEX_Display hex_display_1 (.A(A), .out_2(hex_display_1_out_2));
  HEX_Display hex_display_2 (.A(ALUout[3:0]), .out_2(hex_display_2_out_2));
  operation0 operation0_1 (.A(A), .ALUout(operation0_1_aluout));
  operation1 operation1_1 (.A(A), .B(ALUout[3:0]), .ALUout(operation1_1_aluout));
  operation2 operation2_1 (.A(A), .B(ALUout[3:0]), .ALUout(operation2_1_aluout));
  operation3 operation3_1 (.A(A), .B(ALUout[3:0]), .ALUout(operation3_1_aluout));
  operation4 operation4_1 (.A(A), .B(ALUout[3:0]), .ALUout(operation4_1_aluout));
  newoperation5 newoperation5_1 (.B(ALUout[3:0]), .A(A), .ALUout(newoperation5_1_aluout));
  operation6 operation6_1 (.B(ALUout[3:0]), .A(A), .ALUout(operation6_1_aluout));
  operation7 operation7_1 (.B(ALUout[3:0]), .A(A), .ALUout(operation7_1_aluout));
  Multiplexer #(.enable("false"), .select(3), .width(8)) multiplexer_1 (
    .in0(operation0_1_aluout), .in1(operation1_1_aluout), .in2(operation2_1_aluout),
    .in3(operation3_1_aluout), .in4(operation4_1_aluout), .in5(newoperation5_1_aluout),
    .in6(operation6_1_aluout), .in7(operation7_1_aluout), .out(multiplexer_1_out), .sel(C));
  Register register_1 (.D(multiplexer_1_out), .en(ClearSignals), .clk(Clock), .Q(ALUout), .clr(Reset));
  LED led_1 (.in(ALUout[0]));
  LED led_2 (.in(ALUout[1]));
  LED led_3 (.in(ALUout[2]));
  LED led_4 (.in(ALUout[3]));
  LED led_5 (.in(ALUout[4]));
  LED led_6 (.in(ALUout[5]));
  LED led_7 (.in(ALUout[6]));
  LED led_8 (.in(ALUout[7]));
  HEX_Display Low4 (.A(ALUout[3:0]), .out_2(Low4_out_2));
  HEX_Display High4 (.A(ALUout[7:4]), .out_2(High4_out_2));
  _7_Segment_Display u_7_segment_display_3 (
    .g(High4_out_2[6]), .f(High4_out_2[5]), .a(High4_out_2[0]), .b(High4_out_2[1]), .e(High4_out_2[4]),
    .d(High4_out_2[3]), .c(High4_out_2[2]));  // open: dp
  _7_Segment_Display u_7_segment_display_4 (
    .g(Low4_out_2[6]), .f(Low4_out_2[5]), .a(Low4_out_2[0]), .b(Low4_out_2[1]), .e(Low4_out_2[4]),
    .d(Low4_out_2[3]), .c(Low4_out_2[2]));  // open: dp
endmodule

module D_Latch (
  input  D,
  input  Clock,
  output Q,
  output Q_NOT
);

  wire nand_1_out, nand_2_out, not_1_out;

  not not_1 (not_1_out, D);
  nand nand_1 (nand_1_out, D, Clock);
  nand nand_2 (nand_2_out, Clock, not_1_out);
  nand nand_3 (Q, nand_1_out, Q_NOT);
  nand nand_4 (Q_NOT, Q, nand_2_out);
endmodule

module edge_triggered_D_flip_flop (
  input  D,
  input  Clock,
  output Q
);

  wire d_latch_1_q, not_1_out;

  not not_1 (not_1_out, Clock);
  D_Latch d_latch_1 (.D(D), .Clock(Clock), .Q(d_latch_1_q));  // open: Q_NOT
  D_Latch d_latch_2 (.D(d_latch_1_q), .Clock(not_1_out), .Q(Q));  // open: Q_NOT
endmodule

module shifterbit (
  input  LoadVal,
  input  in_value,
  input  ShiftRight,
  input  Load_n,
  input  clk,
  input  reset,
  output shiftOut
);

  wire multiplexer_1_out, multiplexer_2_out;

  Multiplexer #(.enable("false")) multiplexer_1 (
    .in0(shiftOut), .in1(in_value), .out(multiplexer_1_out), .sel(ShiftRight));
  Multiplexer #(.enable("false")) multiplexer_2 (
    .in0(LoadVal), .in1(multiplexer_1_out), .out(multiplexer_2_out), .sel(Load_n));
  D_Flip_Flop d_ff_1 (.D(multiplexer_2_out), .clk(clk), .Q(shiftOut), .reset(reset));  // open: Qn, preset
endmodule

module shifter_register (
  input  [7:0] LoadVar,
  input  clk,
  input  reset,
  input  Load_n,
  input  ShiftRight,
  input  ASR,
  output [7:0] shifter_out
);

  wire multiplexer_1_out;

  Multiplexer #(.enable("false")) multiplexer_1 (.in0(1'b0), .in1(shifter_out[7]), .out(multiplexer_1_out), .sel(ASR));
  shifterbit shifterbit_1 (
    .LoadVal(LoadVar[0]), .in_value(shifter_out[1]), .ShiftRight(ShiftRight), .Load_n(Load_n), .clk(clk),
    .reset(reset), .shiftOut(shifter_out[0]));
  shifterbit shifterbit_2 (
    .LoadVal(LoadVar[1]), .in_value(shifter_out[2]), .ShiftRight(ShiftRight), .Load_n(Load_n), .clk(clk),
    .reset(reset), .shiftOut(shifter_out[1]));
  shifterbit shifterbit_3 (
    .LoadVal(LoadVar[2]), .in_value(shifter_out[3]), .ShiftRight(ShiftRight), .Load_n(Load_n), .clk(clk),
    .reset(reset), .shiftOut(shifter_out[2]));
  shifterbit shifterbit_4 (
    .LoadVal(LoadVar[3]), .in_value(shifter_out[4]), .ShiftRight(ShiftRight), .Load_n(Load_n), .clk(clk),
    .reset(reset), .shiftOut(shifter_out[3]));
  shifterbit shifterbit_5 (
    .LoadVal(LoadVar[4]), .in_value(shifter_out[5]), .ShiftRight(ShiftRight), .Load_n(Load_n), .clk(clk),
    .reset(reset), .shiftOut(shifter_out[4]));
  shifterbit shifterbit_6 (
    .LoadVal(LoadVar[5]), .in_value(shifter_out[6]), .ShiftRight(ShiftRight), .Load_n(Load_n), .clk(clk),
    .reset(reset), .shiftOut(shifter_out[5]));
  shifterbit shifterbit_7 (
    .LoadVal(LoadVar[6]), .in_value(shifter_out[7]), .ShiftRight(ShiftRight), .Load_n(Load_n), .clk(clk),
    .reset(reset), .shiftOut(shifter_out[6]));
  shifterbit shifterbit_8 (
    .LoadVal(LoadVar[7]), .in_value(multiplexer_1_out), .ShiftRight(ShiftRight), .Load_n(Load_n), .clk(clk),
    .reset(reset), .shiftOut(shifter_out[7]));
endmodule
