// Logisim project CSC258Lab5.circ as structural Verilog: 8 circuits, main circuit main
module main (
  input  SW0,
  input  SW1,
  input  SW2
);

  wire KEY0_out, KEY1_out, part3_1_ledr0;

  Button KEY0 (.out(KEY0_out));
  Button KEY1 (.out(KEY1_out));
  LED led_1 (.in(part3_1_ledr0));
  part3 part3_1 (.KEY0(KEY0_out), .KEY1(KEY1_out), .SW0(SW0), .SW1(SW1), .SW2(SW2), .LEDR0(part3_1_ledr0));
endmodule

module counter8 (
  input  Enable,
  input  Clk,
  input  Clear_b,
  output Q0,
  output Q1,
  output Q2,
  output Q3,
  output Q4,
  output Q5,
  output Q6,
  output Q7
);

  wire and_1_out, and_2_out, and_3_out, and_4_out, and_5_out, and_6_out, and_7_out;

  T_Flip_Flop t_ff_1 (.T(Enable), .clk(Clk), .Q(Q0), .reset(Clear_b));  // open: Qn, preset
  and and_1 (and_1_out, Enable, Q0);
  T_Flip_Flop t_ff_2 (.T(and_1_out), .clk(Clk), .Q(Q1), .reset(Clear_b));  // open: Qn, preset
  and and_2 (and_2_out, and_1_out, Q1);
  T_Flip_Flop t_ff_3 (.T(and_2_out), .clk(Clk), .Q(Q2), .reset(Clear_b));  // open: Qn, preset
  and and_3 (and_3_out, and_2_out, Q2);
  T_Flip_Flop t_ff_4 (.T(and_3_out), .clk(Clk), .Q(Q3), .reset(Clear_b));  // open: Qn, preset
  Hex_Digit_Display hex_digit_display_1 (.value({Q3, Q2, Q1, Q0}));  // open: dp
  and and_4 (and_4_out, and_3_out, Q3);
  Hex_Digit_Display hex_digit_display_2 (.value({Q7, Q6, Q5, Q4}));  // open: dp
  T_Flip_Flop t_ff_5 (.T(and_4_out), .clk(Clk), .Q(Q4), .reset(Clear_b));  // open: Qn, preset
  and and_5 (and_5_out, and_4_out, Q4);
  T_Flip_Flop t_ff_6 (.T(and_5_out), .clk(Clk), .Q(Q5), .reset(Clear_b));  // open: Qn, preset
  and and_6 (and_6_out, and_5_out, Q5);
  T_Flip_Flop t_ff_7 (.T(and_6_out), .clk(Clk), .Q(Q6), .reset(Clear_b));  // open: Qn, preset
  and and_7 (and_7_out, and_6_out, Q6);
  T_Flip_Flop t_ff_8 (.T(and_7_out), .clk(Clk), .Q(Q7), .reset(Clear_b));  // open: Qn, preset
endmodule

module RateDivider (
  input  reset,
  input  Clk,
  input  SW0,
  input  SW1,
  output slowingClk
);

  wire [7:0] multiplexer_1_out;

  Multiplexer #(.enable("false"), .select(2), .width(8)) multiplexer_1 (
    .in0(8'h1), .in1(8'h1f), .in2(8'h3f), .in3(8'h7f), .out(multiplexer_1_out), .sel({SW1, SW0}));
  Counter #(.ongoal("load")) counter_1 (
    .clr(reset), .load(1'b0), .up(1'b0), .clk(Clk), .D(multiplexer_1_out), .carry(slowingClk));  // open: count, Q
endmodule

module DisplayCounter (
  input  Enable,
  input  Clk,
  input  Clear_b,
  output [3:0] digit4output
);

  wire and_1_out, and_2_out, and_3_out;

  T_Flip_Flop t_ff_1 (.T(Enable), .clk(Clk), .Q(digit4output[0]), .reset(Clear_b));  // open: Qn, preset
  and and_1 (and_1_out, Enable, digit4output[0]);
  T_Flip_Flop t_ff_2 (.T(and_1_out), .clk(Clk), .Q(digit4output[1]), .reset(Clear_b));  // open: Qn, preset
  and and_2 (and_2_out, and_1_out, digit4output[1]);
  T_Flip_Flop t_ff_3 (.T(and_2_out), .clk(Clk), .Q(digit4output[2]), .reset(Clear_b));  // open: Qn, preset
  and and_3 (and_3_out, and_2_out, digit4output[2]);
  T_Flip_Flop t_ff_4 (.T(and_3_out), .clk(Clk), .Q(digit4output[3]), .reset(Clear_b));  // open: Qn, preset
endmodule

module part2 (
  input  clear,
  input  SW0,
  input  SW1,
  input  Enable
);

  wire clock_1_out, ratedivider_1_slowingclk;
  wire [3:0] displaycounter_1_digit4output, TestIfSlowComparsion_q0, TestIfSlowComparsion_q4;

  Clock clock_1 (.out(clock_1_out));
  RateDivider ratedivider_1 (
    .reset(clear), .Clk(clock_1_out), .SW0(SW0), .SW1(SW1), .slowingClk(ratedivider_1_slowingclk));
  counter8 TestIfSlowComparsion (
    .Enable(Enable), .Clk(clock_1_out), .Clear_b(clear), .Q0(TestIfSlowComparsion_q0[0]),
    .Q1(TestIfSlowComparsion_q0[1]), .Q2(TestIfSlowComparsion_q0[2]), .Q3(TestIfSlowComparsion_q0[3]),
    .Q4(TestIfSlowComparsion_q4[0]), .Q5(TestIfSlowComparsion_q4[1]), .Q6(TestIfSlowComparsion_q4[2]),
    .Q7(TestIfSlowComparsion_q4[3]));
  Hex_Digit_Display hex_digit_display_1 (.value(TestIfSlowComparsion_q4));  // open: dp
  Hex_Digit_Display hex_digit_display_2 (.value(TestIfSlowComparsion_q0));  // open: dp
  DisplayCounter displaycounter_1 (
    .Enable(ratedivider_1_slowingclk), .Clk(clock_1_out), .Clear_b(clear),
    .digit4output(displaycounter_1_digit4output));
  Hex_Digit_Display HEX0 (.value(displaycounter_1_digit4output));  // open: dp
endmodule

module part3 (
  input  KEY0,
  input  KEY1,
  input  SW0,
  input  SW1,
  input  SW2,
  output LEDR0
);

  wire shift_register_1_p3;
  wire [15:0] shift_register_1_p6;

  // Shift_Register #(.length(16)) shift_register_1: pin names not known; wires that end beside it: KEY0, KEY1, shift_register_1_p3, shift_register_1_p3, 1'b0, shift_register_1_p6[0], shift_register_1_p6[1], shift_register_1_p6[2], shift_register_1_p6[3], shift_register_1_p6[4], shift_register_1_p6[5], shift_register_1_p6[6], shift_register_1_p6[7], shift_register_1_p6[8], shift_register_1_p6[9], shift_register_1_p6[10], shift_register_1_p6[11]
  clkhalf clkhalf_1 (.Clear(KEY0), .slowingClk(shift_register_1_p3));
  LUT lut_1 (.SW0(SW0), .SW1(SW1), .SW2(SW2), .Lout(shift_register_1_p6));
endmodule

module LUT (
  input  SW0,
  input  SW1,
  input  SW2,
  output [15:0] Lout
);

  Multiplexer #(.enable("false"), .select(3), .width(16)) multiplexer_1 (
    .in0(16'ha800), .in1(16'he000), .in2(16'hae00), .in3(16'hab80), .in4(16'hbb80), .in5(16'heae0),
    .in6(16'hebb8), .in7(16'heea0), .out(Lout), .sel({SW2, SW1, SW0}));
endmodule

module clkhalf (
  input  Clear,
  output slowingClk
);

  wire clock_1_out;

  Counter #(.max('h1), .ongoal("load"), .width(1)) counter_1 (
    .clr(Clear), .load(1'b0), .up(1'b0), .clk(clock_1_out), .D(1'b1), .carry(slowingClk));  // open: count, Q
  Clock clock_1 (.out(clock_1_out));
endmodule
